// Logisim project pc.circ as structural Verilog: 3 circuits, main circuit Computer
module main (
  input  [15:0] in_1,
  output [7:0] out_2,
  output out_3,
  output [15:0] out_4,
  output [15:0] _7,
  output [15:0] _6,
  output [15:0] _5,
  output [15:0] _4,
  output [15:0] _3,
  output [15:0] _2,
  output [15:0] _1,
  output [15:0] _0
);

  wire clock_1_out, decoder_1_out0, decoder_1_out1, decoder_1_out2, decoder_1_out3, decoder_1_out4,
       decoder_1_out5, decoder_1_out6, decoder_1_out7, nand_1_out, reset_out;
  wire [2:0] shifter_1_out_2;
  wire [15:0] adder_1_out, and_1_out, and_2_out, controlled_buffer_1_out, controlled_buffer_2_out,
       demultiplexer_1_out0, demultiplexer_1_out1, demultiplexer_1_out2, demultiplexer_1_out3,
       demultiplexer_1_out4, demultiplexer_1_out5, demultiplexer_1_out6, demultiplexer_1_out7, divider_1_out,
       multiplexer_1_out, multiplexer_2_out, multiplexer_3_out, multiplier_1_out, shifter_1_out,
       subtractor_1_out;

  Button reset (.out(reset_out));
  Counter counter_1 (.Q(out_2), .clk(clock_1_out), .clr(reset_out));  // open: load, D, count, carry
  Demultiplexer #(.select(3), .width(16)) demultiplexer_1 (
    .out0(demultiplexer_1_out0), .out1(demultiplexer_1_out1), .out2(demultiplexer_1_out2),
    .out3(demultiplexer_1_out3), .out4(demultiplexer_1_out4), .out5(demultiplexer_1_out5),
    .out6(demultiplexer_1_out6), .out7(demultiplexer_1_out7), .in(multiplexer_1_out), .sel(shifter_1_out_2),
    .en(1'b1));
  Multiplexer #(.width(16)) multiplexer_1 (
    .in0(out_4), .in1(controlled_buffer_2_out), .out(multiplexer_1_out), .sel(shifter_1_out[11]), .en(1'b1));
  Decoder #(.select(3)) decoder_1 (
    .out0(decoder_1_out0), .out1(decoder_1_out1), .out2(decoder_1_out2), .out3(decoder_1_out3),
    .out4(decoder_1_out4), .out5(decoder_1_out5), .out6(decoder_1_out6), .out7(decoder_1_out7),
    .sel(shifter_1_out_2), .en(1'b1));
  Register #(.width(16)) u__3 (
    .D(demultiplexer_1_out3), .en(decoder_1_out3), .Q(_3), .clk(clock_1_out), .clr(reset_out));
  Register #(.width(16)) u__4 (
    .D(demultiplexer_1_out4), .en(decoder_1_out4), .Q(_4), .clk(clock_1_out), .clr(reset_out));
  assign controlled_buffer_1_out = nand_1_out ? and_1_out : 16'bz;  // Controlled_Buffer controlled_buffer_1
  assign and_1_out = in_1 & ~16'hf;  // AND_Gate and_1, 16 bits wide
  assign and_2_out = in_1 & 16'hf;  // AND_Gate and_2, 16 bits wide
  assign controlled_buffer_2_out = nand_1_out ? and_2_out : 16'bz;  // Controlled_Buffer controlled_buffer_2
  Register #(.width(16)) u__2 (
    .D(demultiplexer_1_out2), .en(decoder_1_out2), .Q(_2), .clk(clock_1_out), .clr(reset_out));
  Register #(.width(16)) u__1 (
    .D(demultiplexer_1_out1), .en(decoder_1_out1), .Q(_1), .clk(clock_1_out), .clr(reset_out));
  Register #(.width(16)) u__6 (
    .D(demultiplexer_1_out6), .en(decoder_1_out6), .Q(_6), .clk(clock_1_out), .clr(reset_out));
  Register #(.width(16)) u__5 (
    .D(demultiplexer_1_out5), .en(decoder_1_out5), .Q(_5), .clk(clock_1_out), .clr(reset_out));
  Clock clock_1 (.out(clock_1_out));
  Shifter #(.width(16), .shift("rr")) shifter_1 (
    .in(controlled_buffer_1_out), .\dist (4'b0100),
    .out({shifter_1_out[15:14], shifter_1_out[15:14], shifter_1_out[11:9], shifter_1_out_2, shifter_1_out[5:0]}));
  Register #(.width(16)) u__0 (
    .D(demultiplexer_1_out0), .en(decoder_1_out0), .Q(_0), .clk(clock_1_out), .clr(reset_out));
  Register #(.width(16)) u__7 (
    .D(demultiplexer_1_out7), .en(decoder_1_out7), .Q(_7), .clk(clock_1_out), .clr(reset_out));
  Multiplexer #(.select(3), .width(16)) multiplexer_2 (
    .in0(_0), .in1(_1), .in2(_2), .in3(_3), .in4(_4), .in5(_5), .in6(_6), .in7(_6), .out(multiplexer_2_out),
    .sel(shifter_1_out[2:0]), .en(1'b1));
  Multiplexer #(.select(3), .width(16)) multiplexer_3 (
    .in0(_0), .in1(_1), .in2(_2), .in3(_3), .in4(_4), .in5(_5), .in6(_6), .in7(_7), .out(multiplexer_3_out),
    .sel(shifter_1_out[5:3]), .en(1'b1));
  Adder #(.width(16)) adder_1 (.a(multiplexer_2_out), .b(multiplexer_3_out), .out(adder_1_out));  // open: cin, cout
  Subtractor #(.width(16)) subtractor_1 (
    .a(multiplexer_2_out), .b(multiplexer_3_out), .out(subtractor_1_out));  // open: bin, bout
  Multiplier #(.width(16)) multiplier_1 (
    .a(multiplexer_2_out), .b(multiplexer_3_out), .out(multiplier_1_out));  // open: cin, cout
  Divider #(.width(16)) divider_1 (
    .a(multiplexer_2_out), .b(multiplexer_3_out), .out(divider_1_out));  // open: upper, rem
  Multiplexer #(.select(2), .width(16)) multiplexer_4 (
    .in0(adder_1_out), .in1(subtractor_1_out), .in2(multiplier_1_out), .in3(divider_1_out), .out(out_4),
    .sel(shifter_1_out[10:9]), .en(1'b1));
  nand nand_1 (nand_1_out, in_1[0], in_1[1], in_1[2], in_1[3], in_1[4], in_1[5], in_1[6], in_1[7], in_1[8], in_1[9], in_1[10], in_1[11], in_1[12], in_1[13], in_1[14], in_1[15]);

  assign out_3 = 1'b1;
  // also tied to GND on the sheet: {shifter_1_out[14], shifter_1_out[15]}
endmodule

module ROM_chip (
  input  [7:0] in_1,
  input  in_2,
  output [15:0] out_3
);

  ROM #(.dataWidth(16)) rom_1 (.addr(in_1), .data(out_3), .sel(in_2));
endmodule

module Computer (
);

  wire clock_1_out, main_1_out_3;
  wire [7:0] main_1_out_2;
  wire [15:0] main_1__0, main_1__1, main_1__2, main_1__3, main_1__4, main_1__5, main_1__6, main_1__7,
       main_1_out_4, rom_1_data;

  Register #(.width(16)) register_1 (.D(main_1__7), .en(1'b1), .clk(clock_1_out));  // open: Q, clr
  ROM #(.dataWidth(16)) rom_1 (.addr(main_1_out_2), .data(rom_1_data), .sel(main_1_out_3));
  main main_1 (
    .in_1(rom_1_data), .out_2(main_1_out_2), .out_3(main_1_out_3), ._3(main_1__3), ._2(main_1__2),
    ._1(main_1__1), ._0(main_1__0), ._4(main_1__4), ._5(main_1__5), ._6(main_1__6), ._7(main_1__7),
    .out_4(main_1_out_4));
  Register #(.width(16)) register_2 (.D(main_1__0), .en(1'b1), .clk(clock_1_out));  // open: Q, clr
  Register #(.width(16)) register_3 (.D(main_1__1), .en(1'b1), .clk(clock_1_out));  // open: Q, clr
  Register #(.width(16)) register_4 (.D(main_1__2), .en(1'b1), .clk(clock_1_out));  // open: Q, clr
  Register #(.width(16)) register_5 (.D(main_1__3), .en(1'b1), .clk(clock_1_out));  // open: Q, clr
  Register #(.width(16)) register_6 (.D(main_1__4), .en(1'b1), .clk(clock_1_out));  // open: Q, clr
  Register #(.width(16)) register_7 (.D(main_1__5), .en(1'b1), .clk(clock_1_out));  // open: Q, clr
  Register #(.width(16)) register_8 (.D(main_1__6), .en(1'b1), .clk(clock_1_out));  // open: Q, clr
  Clock clock_1 (.out(clock_1_out));
  Register #(.width(16)) ALU_result (.D(main_1_out_4), .en(1'b1), .clk(clock_1_out));  // open: Q, clr

  // Notes on the sheet:
  //   contents of rom_1 (hex, n*v repeats v):
  //   800f 840d 880
endmodule
